# Fritzing sketch Mouse_City_Circuit (saved by Fritzing 0.9.9b)
breadboards: 1

parts:
  Part1 = Audio FX Sound Board + 2x2W Amp
  WeMos_D1_Mini1 = WeMos D1 Mini  # not connected
  R1 = Resistor [tolerance=±5% resistance=470 package="1206 [SMD]"]  # not connected
  JP1 = Header 1 [package=1x01_offset]  # not connected
  C1 = Electrolytic Capacitor [capacitance=1000µF voltage=35V package="300 mil [THT, electrolytic]"]
  part = SO-24x [chip_label=SO-24x package=SO(x)]  # not connected
  JP2 = Header 1 [package=1x01_offset]
  JP3 = Header 1 [package=1x01_offset]
  JP4 = Header 1 [package=1x01_offset]
  JP5 = Header 1 [package=1x01_offset]

nets:
  N1: Part1.GND, C1.-, JP2.1, JP4.1
  N2: C1.+, JP3.1, JP5.1

custom parts:
  Audio FX Sound Board + 2x2W Amp: The Adafruit Sound Board, the fastest way to add audio effects to a project!
